# Fritzing sketch Fritzing_Helpmet (saved by Fritzing 0.9.4)
breadboards: 1

parts:
  Part1 = u-blox NEO-6M GPS Breakout
  J1 = Basic Force Sensing Resistor (FSR) [package=THT]
  VCC1 = 9V Battery
  R4 = Resistor [tolerance=±5% resistance=22k package=THT]
  U1 = ESP8266 NodeMCU LoLin module
  SW1 = Slide_Switch_new

nets:
  GND: Part1.GND, VCC1.-, R4.Pin_1, U1.GND
  VCC: Part1.VCC, J1.pin_1, U1.3V3
  N1: Part1.TXD, U1.D2
  N2: Part1.RXD, U1.D1
  N3: J1.pin_0, R4.Pin_0, U1.A0
  N4: VCC1.+, SW1.pin_2
  N5: U1.Vin, SW1.pin_1

custom parts:
  9V Battery: Your standard 9V battery
  ESP8266 NodeMCU LoLin module: ESP8266 based NodeMCU
  Slide_Switch_new: the New two pin slide switch
